# Fritzing sketch dfPlayerESP8266 (saved by Fritzing 0.9.3b)
breadboards: 1

parts:
  part = Resistor [tolerance=±5% resistance=2.2k package=THT]
  U1 = ESP8266 WiFi Module [part_number=ESP8266]
  V1 = DC Power [voltage=4.2]
  part_2 = Voltage Regulator - 3.3V [package="TO220 [THT]"]
  S1 = Toggle Switch [package=THT]
  S2 = Pushbutton [package=THT]
  part_3 = Electrolytic Capacitor [capacitance=0.22mF package="100 mil [THT, electrolytic]"]
  S3 = Pushbutton [package=THT]
  S4 = Pushbutton [package=THT]
  S6 = Pushbutton [package=THT]
  DFPlayer_Mini1 = DFPlayer MINI [package="DIP (Dual Inline) [THT]"]
  SPKR1 = Loudspeaker
  U2 = 3.5mm Audio Jack [package=audio-jack-3.5mm-smd]
  Part1 = Micro Lipo Charger
  JP1 = USB_MICROB_PLUG [package=micro-b-ra-th]
  1 = Resistor [tolerance=±5% resistance=10k package=THT]
  2 = Resistor [tolerance=±5% resistance=47k package=THT]

nets:
  N1: part.Pin_0, U1.GPIO_15, DFPlayer_Mini1.RX
  GND: part.Pin_1, U1.GND, V1.V-, part_2.GND, S2.leg0, part_3.-, S3.leg0, S4.leg0, S6.leg0, DFPlayer_Mini1.GND, U2.SLEEVE, Part1.GND, JP1.GND, 1.Pin_1
  N2: U1.VCC, U1.CH_PD, part_2.output_voltage, part_3.+
  N3: U1.GPIO_4, S2.leg1
  N4: U1.GPIO_5, DFPlayer_Mini1.TX
  N5: U1.ADC_0, 1.Pin_0, 2.Pin_1
  N6: U1.GPIO_14, S6.leg1
  N7: U1.GPIO_12, S3.leg1
  N8: U1.GPIO_13, S4.leg1
  N9: V1.V+, S1.COM, Part1.VBAT
  N10: part_2.input_voltage, S1.L2, DFPlayer_Mini1.VCC, 2.Pin_0
  N11: DFPlayer_Mini1.DAC_R, U2.RIGHT
  N12: DFPlayer_Mini1.DAC_L, U2.LEFT
  N13: DFPlayer_Mini1.SPK1, SPKR1.pin2
  N14: DFPlayer_Mini1.SPK2, SPKR1.pin1
  N15: DFPlayer_Mini1.USB_+, JP1.D+
  N16: DFPlayer_Mini1.USB_-, JP1.D-
  5V: Part1.5V, JP1.VCC

notes:
  dfPlayer ESP8266
  VOL+  VOL-  SEL1  SEL2
  mute

custom parts:
  DFPlayer MINI: MP3 module by DFRobot.com for playing Music from an SD-Card. Supports WAV and MP3 files.
  Micro Lipo Charger: Oh so handy, this little lipo charger is so small and easy to use you can keep it on your desk or mount it easily into any project! Simply plug it via any MicroUSB cable into a USB port and a 3.7V/4.2V lithium polymer or lithium ion rechargeable battery into the JST plug on the other end. There are two LEDs - one red and one green. While charging, the red LED is lit. When the battery is fully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
